# Fritzing sketch Adding_GPIO_Pins_MCP23017 (saved by Fritzing 1.0.2b)
breadboards: 1

parts:
  Part1 = VIDI-X
  Part2 = Adafruit MCP23017 STEMMA QT [part_number="Adafruit #5346"]
  R2 = Resistor [tolerance=±5% power=0.25W resistance=330 package=THT]
  R3 = Resistor [tolerance=±5% power=0.25W resistance=330 package=THT]
  R4 = Resistor [tolerance=±5% power=0.25W resistance=330 package=THT]
  R5 = Resistor [tolerance=±5% power=0.25W resistance=330 package=THT]
  R6 = Resistor [tolerance=±5% power=0.25W resistance=10k package=THT]  # not connected
  R7 = Resistor [tolerance=±5% power=0.25W resistance=10k package=THT]  # not connected
  R8 = Resistor [tolerance=±5% power=0.25W resistance=10k package=THT]  # not connected
  R9 = Resistor [tolerance=±5% power=0.25W resistance=10k package=THT]  # not connected
  LED6 = LED - 5mm [color="Red (660nm)" current=0.030A package="5 mm [THT]"]
  LED7 = LED - 5mm [color="Yellow (585nm)" current=30mA package="5 mm [THT]"]
  LED8 = LED - 5mm [color="Green (560nm)" current=0.030A package="5 mm [THT]"]
  LED9 = LED - 5mm [color="Blue (470nm)" current=0.030A package="5 mm [THT]"]

nets:
  N1: Part1.GND#32, LED6.cathode, LED7.cathode, LED8.cathode, LED9.cathode
  N2: Part1.BTN_A, Part2.GND
  N3: Part1.BTN_B, Part2.VCC
  N4: Part1.3V3, Part2.SDA
  N5: Part1.GND#37, Part2.SCL
  N6: Part2.GPB5, R5.Pin_0, LED7.anode
  N7: Part2.GPB6, R3.Pin_0, LED8.anode
  N8: Part2.GPB7, R4.Pin_0, LED9.anode
  N9: R2.Pin_0, LED6.anode

custom parts:
  VIDI-X: VIDI-X mikroračunalo
  Adafruit MCP23017 STEMMA QT: We’ve gotten a lot of requests for a MCP23017 breakout and we’ve always sorta been like “ehh why not just use the DIP chip?” but with STEMMA QT we could see the use case for a plug and play version that comes with all the passives on board. This Adafruit MCP23017 I2C GPIO Expander Breakout has 16 GPIO with matching ground pad. We particularly like the '17 as an expander for it's simple no-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
